# Fritzing sketch LCD (saved by Fritzing 0.9.3b)
breadboards: 1

parts:
  arduino = Arduino Uno (Rev3)
  LCD1 = LCD screen
  R1 = Resistor [tolerance=±5% resistance=220 package=THT]

nets:
  N1: arduino.D8, LCD1.DB5
  N2: arduino.D12/MISO, LCD1.R/W
  N3: arduino.D2, LCD1.DB6
  N4: arduino.D4, LCD1.DB4
  N5: arduino.D5_PWM, LCD1.DB3
  N6: arduino.D6_PWM, R1.Pin_0
  N7: arduino.D7, LCD1.RS
  5V: arduino.5V, LCD1.VDD, LCD1.V0
  GND: arduino.GND, LCD1.VSS
  N8: LCD1.LED+, R1.Pin_1
