# Fritzing sketch schema (saved by Fritzing 0.9.3b)
breadboards: 1

parts:
  Composant1 = Arduino Uno (Rev3)
  R1 = Photocell (LDR) [package=THT]
  R2 = Resistor [tolerance=±5% resistance=220 package=THT]
  J1 = Piezo Speaker
  LED1 = RGB LED (com. cathode, rgb) [package="5 mm [THT]"]
  R3 = Resistor [tolerance=±5% resistance=220 package=THT]
  LCD1 = LCD screen
  R4 = Resistor [tolerance=±5% resistance=220 package=THT]

nets:
  N1: Composant1.A1, R1.pin_0, R2.Pin_1
  N2: Composant1.D8, LCD1.DB6
  N3: Composant1.D9_PWM, LED1.green_anode
  N4: Composant1.D10_PWM/SS, LED1.red_anode
  N5: Composant1.D11_PWM/MOSI, LED1.blue_anode
  N6: Composant1.D12/MISO, LCD1.E
  N7: Composant1.D13/SCK, J1.pin2
  N8: Composant1.D2, LCD1.DB7
  N9: Composant1.D4, LCD1.DB5
  N10: Composant1.D5_PWM, LCD1.DB4
  N11: Composant1.D6_PWM, R4.Pin_0
  N12: Composant1.D7, LCD1.RS
  5V: Composant1.5V, R1.pin_1, LCD1.VDD
  GND: Composant1.GND, R2.Pin_0, J1.pin1, R3.Pin_0, LCD1.VSS, LCD1.V0, LCD1.R/W, LCD1.LED-
  N13: LED1.common_cathode, R3.Pin_1
  N14: LCD1.LED+, R4.Pin_1
