# Fritzing sketch RVB (saved by Fritzing 0.9.3b)
breadboards: 1

parts:
  LED1 = RGB LED (com. cathode, rgb) [package="5 mm [THT]"]
  arduino = Arduino Uno (Rev3)
  R1 = Resistor [tolerance=±5% resistance=220 package=THT]

nets:
  N1: LED1.red_anode, arduino.D10_PWM/SS
  N2: LED1.common_cathode, R1.Pin_1
  N3: LED1.green_anode, arduino.D11_PWM/MOSI
  N4: LED1.blue_anode, arduino.D9_PWM
  N5: arduino.GND, R1.Pin_0
