# Fritzing sketch photoR (saved by Fritzing 0.9.3b)

parts:
  arduino = Arduino Uno (Rev3)
  R1 = Resistor [tolerance=±5% resistance=220 package=THT]
  photo_resistance = Photocell (LDR) [package=THT]

nets:
  N1: arduino.A1, R1.Pin_1, photo_resistance.pin_0
  N2: arduino.GND, photo_resistance.pin_1
  N3: arduino.5V, R1.Pin_0
