# Fritzing sketch photoR (saved by Fritzing 0.9.3b)
breadboards: 1

parts:
  ArduinoCommande = Arduino Uno (Rev3)
  R1 = Photocell (LDR) [package=THT]
  R2 = Resistor [tolerance=±5% resistance=220 package=THT]

nets:
  N1: ArduinoCommande.A0, R1.pin_0, R2.Pin_1
  N2: ArduinoCommande.GND, R2.Pin_0
  N3: ArduinoCommande.5V, R1.pin_1
